// Logisim project Group work.circ as structural Verilog: 1 circuit, main circuit main
module main (
);

  wire and_1_out, and_2_out, and_3_out, and_4_out, not_1_out, not_2_out, not_3_out, not_4_out, not_5_out,
       not_6_out, not_7_out, not_8_out, not_9_out, or_1_out, undriven, undriven_2, undriven_3, undriven_4,
       undriven_5, undriven_6, undriven_7, undriven_8, undriven_9, undriven_10, undriven_11, undriven_12,
       undriven_13;

  not not_1 (not_1_out, undriven_3);
  not not_2 (not_2_out, undriven_5);
  not not_3 (not_3_out, undriven_6);
  not not_4 (not_4_out, undriven_7);
  not not_5 (not_5_out, undriven_9);
  not not_6 (not_6_out, undriven_10);
  not not_7 (not_7_out, undriven_11);
  not not_8 (not_8_out, undriven_12);
  and and_1 (and_1_out, undriven, undriven_2, not_1_out);
  and and_2 (and_2_out, undriven_4, not_2_out, not_3_out);
  and and_3 (and_3_out, not_4_out, undriven_8, not_5_out);
  and and_4 (and_4_out, not_6_out, not_7_out, not_8_out);
  not not_9 (not_9_out, undriven_13);
  or or_1 (or_1_out, and_1_out, and_2_out, and_3_out, and_4_out);

  // Notes on the sheet:
  //   x
  //   y
  //   x
  //   y
  //   x
  //   y
  //   z
  //   y'
  //   z'
  //   z
  //   x
  //   y
  //   z'
  //   z
  //   z
  //   z
  //   z'
  //   xy'z'
  //   x'
  //   x'
  //   y'
  //   z'
  //   xyz'
  //   x'yz'
  //   x'y'z'
  //   z'
  //   xyz' + xy'z' + x'yz' + x'y'z'
endmodule
